# Fritzing sketch LCDandLCM_Mega (saved by Fritzing 0.9.3b)

parts:
  LCM1602_IIC1 = LCM1602 IIC [part_number="LCM1602 IIC" chip_label="LCM1602 IIC" package="DIP (Dual Inline) [THT]"]
  Part1 = LCD Display 16x2
  Part2 = Arduino Mega 2560 (Rev3)

nets:
  N1: LCM1602_IIC1.VSS, Part1.aún_sin_nombre#0
  N2: LCM1602_IIC1.VDD, Part1.aún_sin_nombre#1
  N3: LCM1602_IIC1.V0, Part1.aún_sin_nombre#2
  N4: LCM1602_IIC1.RS, Part1.aún_sin_nombre#3
  N5: LCM1602_IIC1.RW, Part1.aún_sin_nombre#4
  N6: LCM1602_IIC1.E, Part1.aún_sin_nombre#5
  N7: LCM1602_IIC1.D0, Part1.aún_sin_nombre#6
  N8: LCM1602_IIC1.D1, Part1.aún_sin_nombre#7
  N9: LCM1602_IIC1.D2, Part1.aún_sin_nombre#8
  N10: LCM1602_IIC1.D3, Part1.aún_sin_nombre#9
  N11: LCM1602_IIC1.D4, Part1.aún_sin_nombre#10
  N12: LCM1602_IIC1.D5, Part1.aún_sin_nombre#11
  N13: LCM1602_IIC1.D6, Part1.aún_sin_nombre#12
  N14: LCM1602_IIC1.D7, Part1.aún_sin_nombre#13
  N15: LCM1602_IIC1.A, Part1.aún_sin_nombre#14
  N16: LCM1602_IIC1.K, Part1.aún_sin_nombre#15
  GND: LCM1602_IIC1.GND, Part2.GND
  VCC: LCM1602_IIC1.VCC, Part2.5V
  N17: LCM1602_IIC1.SDA, Part2.SDA
  N18: LCM1602_IIC1.SCL, Part2.SCL
  N19: LCM1602_IIC1.LED_A, LCM1602_IIC1.LED_B

custom parts:
  LCM1602 IIC: I2C-Module to use a 1602 or 2004 LCD on with the wire.h libory Serial LCD Modul
